# Fritzing sketch WiringSchematics (saved by Fritzing 0.9.3b)
circuit board: 9.41194cm x 10.4288cm

parts:
  Arduino_Micro = Arduino Micro (Rev3)
  DHT22 = DHT22 Humidity and Temperature Sensor
  LM1117-3_3 = Voltage Regulator -- 3.3 V -- LM1117
  1N4007_Diode1 = 1N4007 Diode [package=DO-41]
  Relay_module = KY-019 5V Relay Module [package="Breakout board"]
  ESP8266 = ESP8266 WiFi Module [part_number=ESP8266]
  HLK-PM1 = HLK-PM01
  LM393_(Light_sensor) = LM393 LDR breakout [part_number=100027]
  JP1 = Header 2 [package=screwterminal-3.5mm-2_lock]

nets:
  N1: Arduino_Micro.D1/TX, 1N4007_Diode1.C
  N2: Arduino_Micro.D0/RX, ESP8266.TXD
  GND: Arduino_Micro.GND, DHT22.GND, LM1117-3_3.GND, Relay_module.-, ESP8266.GND, HLK-PM1.-Vo, LM393_(Light_sensor).GND
  N3: Arduino_Micro.D2/SDA, Relay_module.S
  N4: Arduino_Micro.D3/SCL, DHT22.DATA
  N5: Arduino_Micro.VIN, HLK-PM1.+Vo
  N6: Arduino_Micro.5V, LM1117-3_3.IN
  N7: Arduino_Micro.A0, LM393_(Light_sensor).AO
  3V3: Arduino_Micro.3V3, DHT22.VDD, Relay_module.+, LM393_(Light_sensor).VCC
  N8: LM1117-3_3.OUT, ESP8266.VCC, ESP8266.GPIO_0, ESP8266.GPIO_16, ESP8266.CH_PD
  N9: 1N4007_Diode1.A, ESP8266.RXD
  N10: HLK-PM1.AC#0, JP1.1
  N11: HLK-PM1.AC#1, JP1.2

custom parts:
  Voltage Regulator -- 3.3 V -- LM1117: LM1117-3.3 Voltage regulator, 3.3 V output. Note that the pinout order is not the same as LM7805 or LM7833.
  1N4007 Diode: Rectifier diode.
  KY-019 5V Relay Module: KY-019 5V Relay module, used to control AC circuits.
  ESP8266 WiFi Module: Generic WiFi Module based on the ESP8266 with onboard PCB antenna and UART communications

// code stored in the sketch: Crepuscular.ino
#include <PubSubClient.h>
#include <WiFiEspUdp.h>
#include <WiFiEspServer.h>
#include <WiFiEspClient.h>
#include <WiFiEsp.h>

#pragma region Settings
char* ssid = "SkyNet";
char* key = "1qazse4rfvgy7ujm";
IPAddress ipaddress(192, 168, 1, 11);
IPAddress server (192, 168, 1, 8);
int port = 1883;
char* user = "mqttuser";
char* password = "Pandora412";
char* topicState = "sensor/crep/relay/0";
char* topicAvailability = "sensor/crep/online";
char* topicRelayCommand = "sensor/crep/relay/0/command";
char* topicCrepuscularCommand = "sensor/crep/command";
char* topicBrightness = "sensor/crep/info/bright";
char* topicTemperature = "sensor/crep/info/temp";
char* topicHumidity = "sensor/crep/info/hum";

const long intervalTemp = 10 * 60000;
const long intervalLight = 5 * 60000;
const long intervalState = 0.5 * 60000;
const long intervalMQTT = 100;

const float tempThreshold = 1;
const float humThreshold = 0.5;
#pragma endregion

#pragma region PIN Settings
const int pinRele = 2;
const int pinTemp = 3;
const int pinLight = A0;
#pragma endregion

#pragma region Global variables
float temperature = 0;
float humidity = 0;

long lastTemp = -intervalTemp;
long lastLight = -intervalLight;
long lastMQTT = -intervalMQTT;
long lastState = -intervalState;

String relePrevState = "off";

float lastTempValue = 0;
float lastHumValue = 0;
#pragma endregion

void setup() {
  Serial.begin (115200);
  pinMode(LED_BUILTIN, OUTPUT);

  releSetOutputPin (pinRele);
  tempSetInputPin (pinTemp);
  lightSetInputPin (pinLight);
  digitalWrite (LED_BUILTIN, HIGH);
  releStateChange(HIGH);
  
  MQTTInit(ssid, key, ipaddress, server, port, user, password);
  MQTTSubscribe (topicRelayCommand);
  MQTTSubscribe (topicCrepuscularCommand);
}

void loop() {
  long currentTime = millis();
  int brightnessValue = 0;
  int err = 0;

  if (currentTime - lastMQTT > intervalMQTT)
  {
    MQTTConnect();
    MQTTLoop();
    lastMQTT = currentTime;
  }

  // Invio messaggio di stato corrente
  if (currentTime - lastState > intervalState)
  {
    char buff[4];
    relePrevState.toCharArray(buff, 4);
    MQTTPublish (topicState,buff); 
    lastState = currentTime;
  }
  
  // Lettura temperatura e umidità
  if (currentTime - lastTemp > intervalTemp)
  {
    if (err = tempReadData (temperature, humidity) == 0)
    {
      //Serial.print (temperature);
      //Serial.print ( " °C - ");
      //Serial.print (humidity);
      //Serial.println (" RH%");
      char buff[8]; // Buffer big enough for 7-character float
      dtostrf(temperature, 0, 2, buff); // Leave room for too large numbers!
      //Serial.println (buff);
      if (temperature < lastTempValue -  tempThreshold || temperature > lastTempValue + tempThreshold)
      { 
        MQTTPublish (topicTemperature, buff);
        lastTempValue = temperature;
      }
      dtostrf(humidity, 0, 2, buff); 
      if (humidity < lastHumValue - humThreshold || humidity > lastHumValue + humThreshold)
      { 
        MQTTPublish (topicHumidity, buff);
        lastHumValue = humidity;
      }
    }
    else
    {
      Serial.print ("Temp. read error: ");
      Serial.println (err);
    }
    lastTemp = currentTime;
  }

  // Lettura luminosità
  if (currentTime - lastLight > intervalLight)
  {
    brightnessValue = lightReadData ();
    if (brightnessValue != 0)
    {
      //Serial.print (brightnessValue);
      //Serial.println (" Lumens");
 
      char buff[4]; // Buffer big enough for 4-character float
      dtostrf(brightnessValue, 0, 0, buff);
      MQTTPublish (topicBrightness, buff);
    }
    else
    {
      Serial.print ("Brightness read error: ");
      Serial.println (err);
    }
    lastLight = currentTime;
  }
}

void MQTTCallback (String &topic, String &payload)
{
  Serial.println ("Incoming: " + topic + " - " + payload);
  if (topic == topicRelayCommand)
  {
    if (payload == "on")
    {
      if (relePrevState != payload)
      {
         releStateChange(LOW);
         MQTTPublish (topicState, "on");
      }
      relePrevState = "on";
    }
    if (payload == "off")
    {
      if (relePrevState != payload)
      {
        releStateChange(HIGH);
        MQTTPublish (topicState, "off");
      }
      relePrevState = "off";
    }
  }
  if (topic == topicCrepuscularCommand)
  {
    if (payload == "announce") MQTTPublish (topicAvailability, "true");
  }
}

// code stored in the sketch: modLightSensor.ino
int lightInputPin;

// *****************************************************
//  Function name:  lightSetInputPin
//  Params:         pinNum - Pin where's the sensor is connected
//  Return value:   None
// *****************************************************
void lightSetInputPin (int pinNum)
{
  lightInputPin = pinNum  ;
}

// *****************************************************
//  Function name:  lightReadData
//  Params:         none
//  Return value:   Value read
// *****************************************************
int lightReadData ()
{
  return analogRead (lightInputPin);
}

// code stored in the sketch: modMQTT.ino
#include <WiFiEsp.h>
#include <PubSubClient.h>

WiFiEspClient espClient;
PubSubClient mqttClient (espClient);

char* mqttSsid;
char* mqttKey;
char* mqttServer;
int mqttPort;
char* mqttUser;
char* mqttPassword;

String mqttTopicsList;

void MQTTInit (char* ssid, char* key, IPAddress staticIP, IPAddress server, int port, char* user, char* password)
{
  Serial1.begin (115200);

  // Initialize ESP Module
  WiFi.init (&Serial1);
  WiFi.config (staticIP);
  WiFi.begin (ssid, key);

  Serial.println ("Checking WiFi...");
  while (WiFi.status() != WL_CONNECTED)
  {
    Serial.println(".");
    delay(1000);
  }
  Serial.println ("WiFi connected");

  mqttUser = user;
  mqttPassword = password;
  mqttClient.setServer(server, port);
  mqttClient.setCallback (messageReceived);
  
  // Allow the hardware to sort itself out
  delay(1500);
}

void MQTTPublish (char* topic, char* message)
{
  mqttClient.publish (topic, message);
}

void MQTTSubscribe (char* topic)
{
  mqttTopicsList = mqttTopicsList + topic + "|";
}

void MQTTConnect()
{
  // Loop until connection
  while (!mqttClient.connected ())
  {
    Serial.println ("Attempting to MQTT connection...");

    if (mqttClient.connect("Crepuscular", mqttUser, mqttPassword, topicAvailability, 0, false, "false"))
    {
      Serial.println ("MQTT Connected");
      
      int iPosDelim = 0;
      int iPosStart = 0;
  
      Serial.println("Topic subscribed: ");    
      do
      {
        iPosDelim = mqttTopicsList.indexOf("|", iPosStart);
        if (iPosDelim > (iPosStart + 1))
        {
          char topic[30];
          int topicLength;
          topicLength = mqttTopicsList.substring(iPosStart, iPosDelim).length() + 1;
          mqttTopicsList.substring(iPosStart, iPosDelim).toCharArray (topic, topicLength);
          
          Serial.println(topic);
          
          mqttClient.subscribe (topic);
          iPosStart = iPosDelim + 1;
        }      
      }
      while (iPosDelim >= 0);

      delay (1000);
      MQTTPublish (topicAvailability, "true");
    }
    else
    {
      Serial.print ("Failed, rc=");
      Serial.print(mqttClient.state());
      Serial.println(" - Retry in 5 seconds");
      // Wait 5 seconds before retrying
      delay(5000);
    }
  }
}

void MQTTLoop()
{
  mqttClient.loop();
}

void messageReceived(char* topic, byte* payload, unsigned int length)
{
  String strTopic(topic);
  String strPayload;

  for (int i = 0; i < length; i++)
  {
    strPayload += " ";
    strPayload[i] = ((char)payload[i]);
  }
  
  MQTTCallback (strTopic, strPayload);
}

// code stored in the sketch: modRelays.ino
int outputPin;

// *****************************************************
//  Function name:  releSetOuputPin
//  Params:         pinNum - Pin where's the sensor is connected
//  Return value:   None
// *****************************************************
void releSetOutputPin (int pinNum)
{
  outputPin = pinNum  ;
  pinMode (outputPin, OUTPUT);
}

// *****************************************************
//  Function name:  releStateChange
//  Params:         state - Relè state (HIGH/LOW - 1/0) 
//  Return value:   None
// *****************************************************
void releStateChange (int state)
{
  digitalWrite (outputPin, state);
}

// code stored in the sketch: modTempDHT22.ino
#include <SimpleDHT.h>

SimpleDHT22 dht22;
int tempInputPin;

// *****************************************************
//  Function name:  tempSetInputPin
//  Params:         pinNum - Pin where's the sensor is connected
//  Return value:   None
// *****************************************************
void tempSetInputPin (int pinNum)
{
  tempInputPin = pinNum  ;
}

// *****************************************************
//  Function name:  tempReadData
//  Params:         temperature - Temp value read
//                  humidity - Humidity value read
//  Return value:   Error code (0 if no error)
// *****************************************************
int tempReadData (float &temperature, float &humidity)
{
  temperature = 5;
  int err = SimpleDHTErrSuccess;
  if ((err = dht22.read2 (tempInputPin, &temperature, &humidity, NULL)) != SimpleDHTErrSuccess)
  {
    return err;
  }
  else
  {
    return 0; 
  }
}
